# Fritzing sketch ArduinoRaspberrypi (saved by Fritzing 0.9.3b)

parts:
  Arduino = Arduino Uno (Rev3)
  Raspberry_Pi = Raspberry Pi B+
  USB_to_UART = USB Connectors [package=usb-a-h]
  BNC_to_Camera = BNC [package=bnc]

nets:
  GND: Arduino.GND, Raspberry_Pi.GND, USB_to_UART.D-, BNC_to_Camera.GND
  N1: Arduino.D4, BNC_to_Camera.OUT
  N2: Arduino.D5_PWM, Raspberry_Pi.GPIO22
  N3: Arduino.D6_PWM, Raspberry_Pi.GPIO23
  N4: Raspberry_Pi.GPIO15, USB_to_UART.GND
  N5: Raspberry_Pi.GPIO14, USB_to_UART.VBUS
  N6: Raspberry_Pi.5V, USB_to_UART.D+
