# Fritzing sketch ArduinoTeensy (saved by Fritzing 0.9.3b)
breadboards: 1

parts:
  Arduino = Arduino Uno (Rev3)
  Teensy = Teensy 3.1
  BNC_to_Camera = BNC [package=bnc]
  Sensor_2 = DIP - 8 pins [chip_label=IC package="DIP (Dual Inline) [THT]"]

nets:
  GND: Arduino.GND, Teensy.GND, BNC_to_Camera.GND, Sensor_2.DG, Sensor_2.AG
  N1: Arduino.D4, BNC_to_Camera.OUT
  N2: Arduino.D5_PWM, Teensy.D4
  N3: Arduino.D6_PWM, Teensy.D3
  N4: Teensy.D11, Sensor_2.MO
  N5: Teensy.D12, Sensor_2.MI
  N6: Teensy.D13, Sensor_2.SC
  N7: Teensy.A6/D20, Sensor_2.SS
  N8: Teensy.3V3, Sensor_2.VI

custom parts:
  DIP - 8 pins: A DIP stand-in part for whatever IC you want. With 8 pins on a 300mil dual inline package (DIP) footprint.
