# Fritzing sketch teensy32_audio (saved by Fritzing 0.9.3b)
breadboards: 1

parts:
  Teensy_3_2 = Teensy 3.2
  U1 = BNC [package=bnc]
  Teensy_3_3 = Prop shield

nets:
  GND: Teensy_3_2.GND, Teensy_3_2.AGND, U1.GND
  N1: Teensy_3_2.D4, U1.OUT
  N2: Teensy_3_3.GND, Teensy_3_3.5Vpower

custom parts:
  Teensy 3.2: The Teensy is a complete USB-based microcontoller development system, in a very small footprint, capable of implementing many types of projects. All programming is done via the USB port. No special programmer is needed, only a standard micro-USB cable and a PC or Macintosh with a USB port. It has a USB keyboard/mouse/joystick emulation stack and can be programmed through Arduino IDE.
  Prop shield: The Prop Shield is meant for making interactive light and sound effects on small handheld props and wearable costumes. Motion Sensors - Allows motion interactive light & sound. Audio Amplifier - Clear quality audio output to a small speaker. Fast LED Driver - Drive APA102 / Dotstar LEDs for colorful lighting with rapid response. Flash Memory - 8 Mbyte storage for images, sound clips, and data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
