# Fritzing sketch teensy32_motionsensors (saved by Fritzing 0.9.3b)
breadboards: 1

parts:
  ADNS-1 = ADNS-9800 8 PINs [chip_label=ADNS-9800 package="DIP (Dual Inline) [THT]"]
  ADNS-2 = ADNS-9800 8 PINs [chip_label=ADNS-9800 package="DIP (Dual Inline) [THT]"]
  Teensy_3_2 = Teensy 3.2
  U1 = BNC [package=bnc]

nets:
  N1: ADNS-1.MISO, ADNS-2.MISO, Teensy_3_2.D12
  N2: ADNS-1.MOSI, ADNS-2.MOSI, Teensy_3_2.D11
  N3: ADNS-1.SS, Teensy_3_2.A6/D20
  N4: ADNS-1.SCK, ADNS-2.SCK, Teensy_3_2.D13
  GND: ADNS-1.AGND, ADNS-1.DGND, ADNS-2.AGND, ADNS-2.DGND, Teensy_3_2.GND, Teensy_3_2.AGND, U1.GND
  VIN: ADNS-1.VIN, ADNS-2.VIN, Teensy_3_2.3V3
  N5: ADNS-2.SS, Teensy_3_2.A7/D21
  N6: Teensy_3_2.D4, U1.OUT

custom parts:
  Teensy 3.2: The Teensy is a complete USB-based microcontoller development system, in a very small footprint, capable of implementing many types of projects. All programming is done via the USB port. No special programmer is needed, only a standard micro-USB cable and a PC or Macintosh with a USB port. It has a USB keyboard/mouse/joystick emulation stack and can be programmed through Arduino IDE.
